# Fritzing sketch dalek-mega (saved by Fritzing 0.9.3b)

parts:
  X1 = DB9 Connector [package=db9]
  Mod1 = L298N DC motor driver
  Power_plug2 = Power plug
  LED1 = smd LED [color="Red (633nm)" package="1206 [SMD]"]
  LED2 = smd LED [color="Red (633nm)" package="1206 [SMD]"]
  R8 = Rotary Potentiometer (Small) [maximum_resistance=100kΩ package=THT]
  R9 = Rotary Potentiometer (Small) [maximum_resistance=100kΩ package=THT]
  R10 = Rotary Potentiometer (Small) [maximum_resistance=100kΩ package=THT]
  R11 = Rotary Potentiometer (Small) [maximum_resistance=100kΩ package=THT]
  R12 = Rotary Potentiometer (Small) [maximum_resistance=100kΩ package=THT]
  S2 = Pushbutton [package="[THT]"]
  S3 = Pushbutton [package="[THT]"]
  R13 = Rotary Potentiometer (Small) [maximum_resistance=100kΩ package=THT]
  U1 = Module 4 Relais 5V [package="Module 4 Relais 5V"]
  Part1 = Arduino Mega 2560 (Rev3)

nets:
  N1: X1.1, U1.K1-NO
  N2: X1.3, U1.K2-NO
  N3: X1.4, U1.K3-NO
  12V: Mod1.12V, Mod1.5V-ENA-JMP-I, Mod1.5V-ENA-JMP-O, Power_plug2.VCC, U1.K4-NF
  GND: Mod1.GND, Power_plug2.GND, LED1.cathode, LED2.cathode
  N4: LED1.anode, LED2.anode, U1.K4-NO
  VCC: R8.leg1, R9.leg1, R10.leg1, R11.leg1, R12.leg1, R13.leg1, U1.VCC, Part1.5V
  N5: R8.wiper, Part1.A2
  GND_2: R8.leg2, R9.leg2, R10.leg2, R11.leg2, R12.leg2, S2.Pin_3, S2.Pin_4, S3.Pin_3, S3.Pin_4, R13.leg2, U1.GND, U1.K1-NF, U1.K2-NF, U1.K3-NF, Part1.GND
  N6: R9.wiper, Part1.A1
  N7: R10.wiper, Part1.A0
  N8: R11.wiper, Part1.A4
  N9: R12.wiper, Part1.A5
  N10: S2.Pin_1, S2.Pin_2, Part1.A3
  N11: S3.Pin_1, S3.Pin_2, Part1.A7
  N12: R13.wiper, Part1.A6
  N13: U1.IN1, Part1.D5_PWM
  N14: U1.IN2, Part1.D4_PWM
  N15: U1.IN3, Part1.D3_PWM
  N16: U1.IN4, Part1.D2_PWM

custom parts:
  L298N DC motor driver: 2x DC motor driver with 78M05 positive voltage regulator (7..35 V) L298N: max 46 V, 2 A Set 5 V Enable jumper to enable 5 V regultor (needed for the L298N) and +5 V output at screw terminal or supply external +5 V at screw terminal Set ENA and/or ENB to +5 V to enable motor permanently or supply ENA and/or ENB with PWM signal IN1 and IN2 set rotation directory for motor A (OUT1/OUT2) IN2 and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
  Module 4 Relais 5V: Module 4 Relais 5V 4x SPD-06VDC-SD-C
