# Fritzing sketch dalek (saved by Fritzing 0.9.3b)
circuit board: 8.46667cm x 5.64444cm
breadboards: 1

parts:
  Part1 = Arduino Uno (Rev3)
  Q1 = NPN-Transistor [package="TO92 [THT]"]
  R1 = Resistor [tolerance=±5% resistance=1k package=THT]
  R2 = Resistor [tolerance=±5% resistance=1k package=THT]
  R3 = Resistor [tolerance=±5% resistance=1k package=THT]
  R4 = Resistor [tolerance=±5% resistance=1k package=THT]
  Q2 = NPN-Transistor [package="TO92 [THT]"]
  Q3 = NPN-Transistor [package="TO92 [THT]"]
  Q4 = NPN-Transistor [package="TO92 [THT]"]
  R5 = Rotary Potentiometer (Small) [maximum_resistance=100kΩ package=THT]
  R6 = Rotary Potentiometer (Small) [maximum_resistance=100kΩ package=THT]
  Power_plug1 = Power plug
  R7 = Rotary Potentiometer (Small) [maximum_resistance=100kΩ package=THT]
  S1 = Pushbutton [package="[THT]"]
  Power_plug2 = Power plug
  Mod1 = L298N DC motor driver
  M1 = Stepper Motor - Bipolar
  OMRON1 = Relay [part_number=FRS1B-S package=THT]
  OMRON2 = Relay [part_number=FRS1B-S package=THT]
  OMRON3 = Relay [part_number=FRS1B-S package=THT]
  OMRON4 = Relay [part_number=FRS1B-S package=THT]
  J1 = Screw terminal - 2 pins [package=THT]

nets:
  N1: Part1.A0, R5.wiper
  N2: Part1.A1, R6.wiper
  N3: Part1.A2, R7.wiper
  N4: Part1.A3, S1.Pin_1, S1.Pin_2
  N5: Part1.D8, Mod1.IN1
  N6: Part1.D9_PWM, Mod1.IN2
  N7: Part1.D10_PWM/SS, Mod1.IN3
  N8: Part1.D11_PWM/MOSI, Mod1.IN4
  GND: Part1.GND, Q1.E, Q2.E, Q3.E, Q4.E, R5.leg2, R6.leg2, R7.leg2, S1.Pin_3, S1.Pin_4, Power_plug2.GND, OMRON2.C1, OMRON2.C2, OMRON3.C1, OMRON3.C2, OMRON4.C1, OMRON4.C2
  N9: Part1.D2, R4.Pin_0
  N10: Part1.D3_PWM, R3.Pin_0
  N11: Part1.D4, R2.Pin_0
  N12: Part1.D5_PWM, R1.Pin_0
  N13: Part1.3V3, R5.leg1, R6.leg1, R7.leg1, OMRON1.COIL1, OMRON2.COIL1, OMRON3.COIL1, OMRON4.COIL1
  VIN: Part1.VIN, Power_plug2.VCC
  N14: Q1.B, R1.Pin_1
  N15: Q1.C, OMRON4.COIL2
  N16: R2.Pin_1, Q3.B
  N17: R3.Pin_1, Q2.B
  N18: R4.Pin_1, Q4.B
  N19: Q2.C, OMRON2.COIL2
  N20: Q3.C, OMRON3.COIL2
  N21: Q4.C, OMRON1.COIL2
  GND_2: Power_plug1.GND, Mod1.GND, J1.pin2
  VCC: Power_plug1.VCC, Mod1.12V, OMRON1.C1, OMRON1.C2
  N22: Mod1.OUT1, M1.C
  N23: Mod1.OUT2, M1.A
  N24: Mod1.OUT3, M1.D
  N25: Mod1.OUT4, M1.B
  N26: Mod1.+5V-J1, Mod1.+5V-J2, Mod1.ENA, Mod1.ENB
  N27: OMRON1.A, J1.pin1

custom parts:
  L298N DC motor driver: 2x DC motor driver with 78M05 positive voltage regulator (7..35 V) L298N: max 46 V, 2 A Set 5 V Enable jumper to enable 5 V regultor (needed for the L298N) and +5 V output at screw terminal or supply external +5 V at screw terminal Set ENA and/or ENB to +5 V to enable motor permanently or supply ENA and/or ENB with PWM signal IN1 and IN2 set rotation directory for motor A (OUT1/OUT2) IN2 and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

// code stored in the sketch: joystick.ino
#include <Stepper.h>

const int stepsPerRevolution = 200;
int stepDelay = 1000;

Stepper myStepper(stepsPerRevolution, 8, 9, 10, 11);

const int joystickXPin = A0;
const int joystickYPin = A1;
const int joystickTwistPin = A2;
const int joystickButtonPin = A3;
bool buttonState = false;

int joystickXValue = 0;
int joystickYValue = 0;
int joystickTwistValue = 0;
int joystickButtonValue = 0;

const int relayUpPin = 2;
const int relayLeftPin = 3;
const int relayRightPin = 4;
const int relayLightsPin = 5;

const int threshold = 100;

void setup()
{
  pinMode(relayUpPin, OUTPUT);
  pinMode(relayLeftPin, OUTPUT);
  pinMode(relayRightPin, OUTPUT);
  pinMode(relayLightsPin, OUTPUT);

  digitalWrite(relayUpPin, HIGH);
  digitalWrite(relayLeftPin, HIGH);
  digitalWrite(relayRightPin, HIGH);
  digitalWrite(relayLightsPin, HIGH);

  pinMode(joystickButtonPin, INPUT_PULLUP);
  
  myStepper.setSpeed(50);
  
  Serial.begin(9600);
}

//void loop()
//{
//  digitalWrite(2, HIGH);
//  delay(500);
//  digitalWrite(2, LOW);
//  delay(500);
//  
//}

void loop()
{
  joystickXValue = analogRead(joystickXPin);
  joystickYValue = analogRead(joystickYPin);
  joystickTwistValue = analogRead(joystickTwistPin);
  joystickButtonValue = analogRead(joystickButtonPin);
  
  Serial.print("Joystick: X = ");
  Serial.println(joystickXValue);
  Serial.print("Joystick: Y = ");
  Serial.println(joystickYValue);
  Serial.print("Joystick: Twist = ");
  Serial.println(joystickTwistPin);
  Serial.print("Joystick: Button = ");
  Serial.println(joystickButtonPin);

  digitalWrite(relayUpPin, HIGH);
  digitalWrite(relayLeftPin, HIGH);
  digitalWrite(relayRightPin, HIGH);

  if (joystickButtonValue < 500)
  {
    buttonState = !buttonState;
  }

  if (joystickYValue > (512 + threshold))
  {
    digitalWrite(relayUpPin, LOW);
    Serial.println("Up: ON");
  }
    else if (joystickXValue > (512 + threshold))
  {
    digitalWrite(relayRightPin, LOW);
    Serial.println("Right: ON");
  }
    else if (joystickXValue < (512 - threshold))
  {
    digitalWrite(relayLeftPin, LOW);
    Serial.println("Left: ON");
  }

  if (joystickTwistValue > 700)
  {
    myStepper.step(stepsPerRevolution);
    Serial.println("clockwise");
    stepDelay = map(joystickTwistValue, 550, 1023, 1000, 200);
  }
  else if(joystickTwistValue < 300)
  {
    myStepper.step(-stepsPerRevolution);
    Serial.println("anti-clockwise");
    stepDelay = map(joystickTwistValue, 450, 0, 1000, 200);
  }
  else
  {
    stepDelay =1000;
    Serial.println("no head movement");
  }  

  if (buttonState == true)
  {
    digitalWrite(relayLightsPin, LOW);
    Serial.println("Lights: ON");
  }
  else if (buttonState == false)
  {
    digitalWrite(relayLightsPin, HIGH);
    Serial.println("Lights: OFF");
  }

  delay(500);  
}
